// Logisim project subtraction & addition.circ as structural Verilog: 20 circuits, main circuit Addition & Subtraction Circuit
module Addition___Subtraction_Circuit (
  input  M0,
  input  B4,
  input  A4,
  input  Bo,
  input  Ao,
  input  B1,
  input  A1,
  input  B2,
  input  A2,
  input  B3,
  input  A3,
  input  Enable,
  output S0,
  output S1,
  output S2,
  output S3,
  output S4,
  output Zero_Flag,
  output Sign_Flag
);

  wire and_1_out, and_2_out, and_3_out, and_4_out, and_5_out, and_6_out, and_7_out, and_8_out, and_11_out,
       and_12_out, n4_bit_parallel_adder_1_c4, n4_bit_parallel_adder_1_s0, n4_bit_parallel_adder_1_s1,
       n4_bit_parallel_adder_1_s2, n4_bit_parallel_adder_1_s3, n4_bit_parallel_adder_2_c4,
       n4_bit_parallel_adder_2_s0, n4_bit_parallel_adder_2_s1, n4_bit_parallel_adder_2_s2,
       n4_bit_parallel_adder_2_s3, not_1_out, not_2_out, not_3_out, not_4_out, not_5_out, not_7_out,
       or_1_out, or_2_out, or_3_out, or_4_out, or_5_out, or_6_out, xor_1_out, xor_2_out, xor_3_out;

  xor xor_1 (xor_1_out, B4, A4);
  xor xor_2 (xor_2_out, M0, xor_1_out);
  and and_1 (and_1_out, Bo, Enable);
  and and_2 (and_2_out, Ao, Enable);
  not not_1 (not_1_out, n4_bit_parallel_adder_1_s0);
  and and_3 (and_3_out, B1, Enable);
  and and_4 (and_4_out, A1, Enable);
  _4_BIT_PARALLEL_ADDER u_4_bit_parallel_adder_1 (
    .S(xor_2_out), .Bo(and_1_out), .Ao(and_2_out), .B1(and_3_out), .A1(and_4_out), .B2(and_5_out),
    .A2(and_6_out), .B3(and_8_out), .A3(and_7_out), .S0(n4_bit_parallel_adder_1_s0),
    .S1(n4_bit_parallel_adder_1_s1), .S2(n4_bit_parallel_adder_1_s2), .S3(n4_bit_parallel_adder_1_s3),
    .C4(n4_bit_parallel_adder_1_c4));
  not not_2 (not_2_out, n4_bit_parallel_adder_1_s1);
  and and_5 (and_5_out, B2, Enable);
  not not_3 (not_3_out, n4_bit_parallel_adder_1_s2);
  and and_6 (and_6_out, A2, Enable);
  para_multiplexer para_multiplexer_1 (
    .Dcurrent3(n4_bit_parallel_adder_1_s0), .in_3(n4_bit_parallel_adder_2_s0),
    .Dcurrent2(n4_bit_parallel_adder_1_s1), .in_5(n4_bit_parallel_adder_2_s1),
    .Dcurrent1(n4_bit_parallel_adder_1_s2), .in_7(n4_bit_parallel_adder_2_s2),
    .Dcurrent0(n4_bit_parallel_adder_1_s3), .in_9(n4_bit_parallel_adder_2_s3), .out_10(S0), .out_11(S1),
    .out_12(S2), .out_13(S3), .Cout_final(or_1_out));
  and and_7 (and_7_out, A3, Enable);
  and and_8 (and_8_out, B3, Enable);
  not not_4 (not_4_out, n4_bit_parallel_adder_1_s3);
  _4_BIT_PARALLEL_ADDER u_4_bit_parallel_adder_2 (
    .S(1'b0), .Bo(1'b1), .Ao(not_1_out), .B1(1'b0), .A1(not_2_out), .B2(1'b0), .A2(not_3_out), .B3(1'b0),
    .A3(not_4_out), .S0(n4_bit_parallel_adder_2_s0), .S1(n4_bit_parallel_adder_2_s1),
    .S2(n4_bit_parallel_adder_2_s2), .S3(n4_bit_parallel_adder_2_s3), .C4(n4_bit_parallel_adder_2_c4));
  not not_5 (not_5_out, xor_2_out);
  and and_9 (S4, n4_bit_parallel_adder_1_c4, not_5_out);
  not not_6 (Zero_Flag, or_3_out);
  not not_7 (not_7_out, n4_bit_parallel_adder_1_c4);
  or or_1 (or_1_out, not_5_out, n4_bit_parallel_adder_1_c4);
  or or_2 (or_2_out, S1, or_5_out);
  or or_3 (or_3_out, S0, or_2_out);
  and and_10 (Sign_Flag, or_3_out, or_6_out);
  and and_11 (and_11_out, A4, n4_bit_parallel_adder_1_c4);
  and and_12 (and_12_out, not_7_out, xor_3_out);
  or or_4 (or_4_out, S3, S4);
  or or_5 (or_5_out, S2, or_4_out);
  or or_6 (or_6_out, and_11_out, and_12_out);
  xor xor_3 (xor_3_out, M0, B4);
endmodule

module ALU (
  input  M0,
  input  M1,
  input  A4,
  input  A3,
  input  A2,
  input  A1,
  input  A0,
  input  B4,
  input  B3,
  input  B2,
  input  B1,
  input  B0,
  output out_13,
  output Zero_Flag,
  output Sign_Flag,
  output S7,
  output S6,
  output S5,
  output S4,
  output S3,
  output S2,
  output S1,
  output S0
);

  wire and_1_out, and_2_out, division_1_div_by_zero, division_1_q0, division_1_q1, division_1_q2,
       division_1_q3, not_1_out, not_2_out, or_1_out, or_2_out, or_3_out, or_4_out, Q0, Q1, Q2, Q3, R0, R1,
       R2, R3, R4, sign_of_Add_Sub, xor_1_out, Z0, Z1, Z2, Z3, Z4, ZA, ZD, ZM;

  not not_1 (not_1_out, M0);
  not not_2 (not_2_out, M1);
  and and_1 (and_1_out, not_1_out, M1);
  and and_2 (and_2_out, M0, M1);
  Division division_1 (
    .Enable(and_2_out), .B3(B3), .B2(B2), .B1(B1), .B0(B0), .A3(A3), .A2(A2), .A1(A1), .A0(A0),
    .Q3(division_1_q3), .Q2(division_1_q2), .Q1(division_1_q1), .Q0(division_1_q0), .Zero_Flag(ZD),
    .Div_by_Zero(division_1_div_by_zero));
  Multiplexer_x multiplexer_x_1 (.S(and_2_out), .I0(1'b0), .I1(division_1_div_by_zero), .out_4(out_13));
  Multiplexer #(.select(2), .enable("false")) multiplexer_1 (
    .in0(ZA), .in1(ZA), .in2(ZM), .in3(ZD), .out(Zero_Flag), .sel({M1, M0}));
  Multiblication multiblication_1 (
    .Enable(and_1_out), .A3(A3), .A2(A2), .A1(A1), .A0(A0), .B0(B0), .B1(B1), .B2(B2), .B3(B3),
    .Zero_Flag(ZM), .Z7(S7), .Z6(S6), .Z5(S5), .Z4(Z4), .Z3(Z3), .Z2(Z2), .Z1(Z1), .Z0(Z0));
  xor xor_1 (xor_1_out, A4, B4);
  and and_3 (Q0, and_2_out, division_1_q0);
  and and_4 (Q1, and_2_out, division_1_q1);
  and and_5 (Q2, division_1_q2, and_2_out);
  and and_6 (Q3, division_1_q3, and_2_out);
  Multiplexer_x multiplexer_x_2 (.S(M1), .I0(sign_of_Add_Sub), .I1(xor_1_out), .out_4(Sign_Flag));
  Addition___Subtraction_Circuit addition_subtraction_circuit_1 (
    .M0(M0), .B4(B4), .A4(A4), .Bo(B0), .Ao(A0), .B1(B1), .A1(A1), .B2(B2), .A2(A2), .B3(B3), .A3(A3),
    .S0(R0), .S1(R1), .S2(R2), .S3(R3), .Zero_Flag(ZA), .S4(R4), .Sign_Flag(sign_of_Add_Sub),
    .Enable(not_2_out));
  or or_1 (or_1_out, R0, Q0);
  or or_2 (or_2_out, R1, Q1);
  or or_3 (or_3_out, R2, Q2);
  or or_4 (or_4_out, R3, Q3);
  or or_5 (S4, R4, Z4);
  or or_6 (S0, or_1_out, Z0);
  or or_7 (S1, or_2_out, Z1);
  or or_8 (S2, or_3_out, Z2);
  or or_9 (S3, or_4_out, Z3);

  // Other names for the same wires on the sheet: Div_by_Zero_Flag = out_13; Z5 = S5; Z6 = S6; Z7 = S7
endmodule

module Project (
  input  A0,
  input  A1,
  input  M1,
  input  M0,
  input  A2,
  input  A3,
  input  A4,
  input  B0,
  input  B1,
  input  B2,
  input  B3,
  input  B4,
  output Div_By_Zero,
  output Zero,
  output Sign
);

  wire alu_1_s0, alu_1_s1, alu_1_s2, alu_1_s3, alu_1_s4, alu_1_s5, alu_1_s6, alu_1_s7,
       bcd_to_7_segment_1_a_2, bcd_to_7_segment_1_b_2, bcd_to_7_segment_1_c_2, bcd_to_7_segment_1_d_2,
       bcd_to_7_segment_1_e, bcd_to_7_segment_1_f, bcd_to_7_segment_1_g, bcd_to_7_segment_2_a_2,
       bcd_to_7_segment_2_b_2, bcd_to_7_segment_2_c_2, bcd_to_7_segment_2_d_2, bcd_to_7_segment_2_e,
       bcd_to_7_segment_2_f, bcd_to_7_segment_2_g, bcd_to_7_segment_3_a_2, bcd_to_7_segment_3_b_2,
       bcd_to_7_segment_3_c_2, bcd_to_7_segment_3_d_2, bcd_to_7_segment_3_e, bcd_to_7_segment_3_f,
       bcd_to_7_segment_3_g, binary_to_bcd_converter_1_out_9, binary_to_bcd_converter_1_z,
       binary_to_bcd_converter_1_z0, binary_to_bcd_converter_1_z0_2, binary_to_bcd_converter_1_z3,
       binary_to_bcd_converter_1_z4, binary_to_bcd_converter_1_z5, binary_to_bcd_converter_1_z6,
       binary_to_bcd_converter_1_z7, binary_to_bcd_converter_1_z8, binary_to_bcd_converter_1_z9,
       binary_to_bcd_converter_1_z10;

  ALU alu_1 (
    .M0(M0), .M1(M1), .B3(B3), .B2(B2), .B1(B1), .B0(B0), .A4(A4), .B4(B4), .A3(A3), .A2(A2), .A1(A1),
    .A0(A0), .S1(alu_1_s1), .S0(alu_1_s0), .S3(alu_1_s3), .S2(alu_1_s2), .S5(alu_1_s5), .S4(alu_1_s4),
    .S7(alu_1_s7), .S6(alu_1_s6), .Zero_Flag(Zero), .Sign_Flag(Sign), .out_13(Div_By_Zero));
  Binary_TO_BCD_CONVERTER binary_to_bcd_converter_1 (
    .a7(alu_1_s7), .a6(alu_1_s6), .a5(alu_1_s5), .a4(alu_1_s4), .a3(alu_1_s3), .a2(alu_1_s2), .a1(alu_1_s1),
    .a0(alu_1_s0), .out_9(binary_to_bcd_converter_1_out_9), .z(binary_to_bcd_converter_1_z),
    .z10(binary_to_bcd_converter_1_z10), .z9(binary_to_bcd_converter_1_z9),
    .z8(binary_to_bcd_converter_1_z8), .z7(binary_to_bcd_converter_1_z7), .z6(binary_to_bcd_converter_1_z6),
    .z5(binary_to_bcd_converter_1_z5), .z4(binary_to_bcd_converter_1_z4), .z3(binary_to_bcd_converter_1_z3),
    .z0(binary_to_bcd_converter_1_z0), .z0_2(binary_to_bcd_converter_1_z0_2));
  BCD_TO_7_SEGMENT bcd_to_7_segment_1 (
    .A(binary_to_bcd_converter_1_out_9), .B(binary_to_bcd_converter_1_z), .C(binary_to_bcd_converter_1_z10),
    .D(binary_to_bcd_converter_1_z9), .a_2(bcd_to_7_segment_1_a_2), .b_2(bcd_to_7_segment_1_b_2),
    .c_2(bcd_to_7_segment_1_c_2), .d_2(bcd_to_7_segment_1_d_2), .e(bcd_to_7_segment_1_e),
    .f(bcd_to_7_segment_1_f), .g(bcd_to_7_segment_1_g));
  _7_Segment_Display u_7_segment_display_1 (
    .g(bcd_to_7_segment_1_g), .f(bcd_to_7_segment_1_f), .a(bcd_to_7_segment_1_a_2),
    .b(bcd_to_7_segment_1_b_2), .e(bcd_to_7_segment_1_e), .d(bcd_to_7_segment_1_d_2),
    .c(bcd_to_7_segment_1_c_2));  // open: dp
  BCD_TO_7_SEGMENT bcd_to_7_segment_2 (
    .A(binary_to_bcd_converter_1_z8), .B(binary_to_bcd_converter_1_z7), .C(binary_to_bcd_converter_1_z6),
    .D(binary_to_bcd_converter_1_z5), .a_2(bcd_to_7_segment_2_a_2), .b_2(bcd_to_7_segment_2_b_2),
    .c_2(bcd_to_7_segment_2_c_2), .d_2(bcd_to_7_segment_2_d_2), .e(bcd_to_7_segment_2_e),
    .f(bcd_to_7_segment_2_f), .g(bcd_to_7_segment_2_g));
  _7_Segment_Display u_7_segment_display_2 (
    .g(bcd_to_7_segment_2_g), .f(bcd_to_7_segment_2_f), .a(bcd_to_7_segment_2_a_2),
    .b(bcd_to_7_segment_2_b_2), .e(bcd_to_7_segment_2_e), .d(bcd_to_7_segment_2_d_2),
    .c(bcd_to_7_segment_2_c_2));  // open: dp
  BCD_TO_7_SEGMENT bcd_to_7_segment_3 (
    .A(binary_to_bcd_converter_1_z4), .B(binary_to_bcd_converter_1_z3), .C(binary_to_bcd_converter_1_z0),
    .D(binary_to_bcd_converter_1_z0_2), .a_2(bcd_to_7_segment_3_a_2), .b_2(bcd_to_7_segment_3_b_2),
    .c_2(bcd_to_7_segment_3_c_2), .d_2(bcd_to_7_segment_3_d_2), .e(bcd_to_7_segment_3_e),
    .f(bcd_to_7_segment_3_f), .g(bcd_to_7_segment_3_g));
  _7_Segment_Display u_7_segment_display_3 (
    .g(bcd_to_7_segment_3_g), .f(bcd_to_7_segment_3_f), .a(bcd_to_7_segment_3_a_2),
    .b(bcd_to_7_segment_3_b_2), .e(bcd_to_7_segment_3_e), .d(bcd_to_7_segment_3_d_2),
    .c(bcd_to_7_segment_3_c_2));  // open: dp
endmodule

module Division (
  input  B3,
  input  B2,
  input  B1,
  input  B0,
  input  A3,
  input  A2,
  input  A1,
  input  A0,
  input  Enable,
  output Zero_Flag,
  output Div_by_Zero,
  output Q3,
  output Q2,
  output Q1,
  output Q0
);

  wire and_1_out, and_2_out, and_3_out, and_4_out, and_5_out, and_6_out, and_7_out, and_9_out, not_4_out,
       para_multiplexer_1_out_10, para_multiplexer_1_out_11, para_multiplexer_1_out_12,
       para_multiplexer_1_out_13, para_multiplexer_2_out_10, para_multiplexer_2_out_11,
       para_multiplexer_2_out_12, para_multiplexer_2_out_13, para_multiplexer_3_out_10,
       para_multiplexer_3_out_11, para_multiplexer_3_out_12, para_multiplexer_3_out_13,
       para_subtractor_1_cout_final, para_subtractor_1_dcurrent0, para_subtractor_1_dcurrent1,
       para_subtractor_1_dcurrent2, para_subtractor_1_dcurrent3, para_subtractor_2_cout_final,
       para_subtractor_2_dcurrent0, para_subtractor_2_dcurrent1, para_subtractor_2_dcurrent2,
       para_subtractor_2_dcurrent3, para_subtractor_3_cout_final, para_subtractor_3_dcurrent0,
       para_subtractor_3_dcurrent1, para_subtractor_3_dcurrent2, para_subtractor_3_dcurrent3,
       para_subtractor_4_cout_final, para_subtractor_4_dcurrent0, para_subtractor_4_dcurrent1,
       para_subtractor_4_dcurrent2, para_subtractor_4_dcurrent3, zero_flag_1_out_5;

  and and_1 (and_1_out, B3, Enable);
  and and_2 (and_2_out, B2, Enable);
  not not_1 (Q3, para_subtractor_1_cout_final);
  and and_3 (and_3_out, B1, Enable);
  and and_4 (and_4_out, B0, Enable);
  para_subtractor para_subtractor_1 (
    .H0(and_4_out), .H1(and_3_out), .H2(and_2_out), .H3(and_1_out), .L0(and_5_out), .L1(1'b0), .L2(1'b0),
    .L3(1'b0), .Dcurrent0(para_subtractor_1_dcurrent0), .Dcurrent1(para_subtractor_1_dcurrent1),
    .Dcurrent2(para_subtractor_1_dcurrent2), .Dcurrent3(para_subtractor_1_dcurrent3),
    .Cout_final(para_subtractor_1_cout_final));
  para_multiplexer para_multiplexer_1 (
    .Dcurrent3(para_subtractor_1_dcurrent3), .in_3(1'b0), .Dcurrent2(para_subtractor_1_dcurrent2),
    .in_5(1'b0), .Dcurrent1(para_subtractor_1_dcurrent1), .in_7(1'b0),
    .Dcurrent0(para_subtractor_1_dcurrent0), .in_9(and_5_out), .out_10(para_multiplexer_1_out_10),
    .out_11(para_multiplexer_1_out_11), .out_12(para_multiplexer_1_out_12),
    .out_13(para_multiplexer_1_out_13), .Cout_final(Q3));
  and and_5 (and_5_out, A3, Enable);
  para_subtractor para_subtractor_2 (
    .H0(and_4_out), .H1(and_3_out), .H2(and_2_out), .H3(and_1_out), .L0(and_6_out),
    .L1(para_multiplexer_1_out_13), .L2(para_multiplexer_1_out_12), .L3(para_multiplexer_1_out_11),
    .Dcurrent0(para_subtractor_2_dcurrent0), .Dcurrent1(para_subtractor_2_dcurrent1),
    .Dcurrent2(para_subtractor_2_dcurrent2), .Dcurrent3(para_subtractor_2_dcurrent3),
    .Cout_final(para_subtractor_2_cout_final));
  not not_2 (Q2, para_subtractor_2_cout_final);
  para_multiplexer para_multiplexer_2 (
    .Dcurrent3(para_subtractor_2_dcurrent3), .in_3(para_multiplexer_1_out_11),
    .Dcurrent2(para_subtractor_2_dcurrent2), .in_5(para_multiplexer_1_out_12),
    .Dcurrent1(para_subtractor_2_dcurrent1), .in_7(para_multiplexer_1_out_13),
    .Dcurrent0(para_subtractor_2_dcurrent0), .in_9(and_6_out), .out_10(para_multiplexer_2_out_10),
    .out_11(para_multiplexer_2_out_11), .out_12(para_multiplexer_2_out_12),
    .out_13(para_multiplexer_2_out_13), .Cout_final(Q2));
  and and_6 (and_6_out, A2, Enable);
  not not_3 (Q1, para_subtractor_3_cout_final);
  para_subtractor para_subtractor_3 (
    .H0(and_4_out), .H1(and_3_out), .H2(and_2_out), .H3(and_1_out), .L0(and_7_out),
    .L1(para_multiplexer_2_out_13), .L2(para_multiplexer_2_out_12), .L3(para_multiplexer_2_out_11),
    .Dcurrent0(para_subtractor_3_dcurrent0), .Dcurrent1(para_subtractor_3_dcurrent1),
    .Dcurrent2(para_subtractor_3_dcurrent2), .Dcurrent3(para_subtractor_3_dcurrent3),
    .Cout_final(para_subtractor_3_cout_final));
  div_by_zero_flag div_by_zero_flag_1 (.in_1(B0), .in_2(B1), .in_3(B2), .in_4(B3), .out_5(Div_by_Zero));
  zero_flag zero_flag_1 (.in_1(A3), .in_2(A2), .in_3(A1), .in_4(A0), .out_5(zero_flag_1_out_5));
  not not_4 (not_4_out, Div_by_Zero);
  and and_7 (and_7_out, A1, Enable);
  and and_8 (Zero_Flag, not_4_out, zero_flag_1_out_5);
  and and_9 (and_9_out, A0, Enable);
  para_multiplexer para_multiplexer_3 (
    .Dcurrent3(para_subtractor_3_dcurrent3), .in_3(para_multiplexer_2_out_11),
    .Dcurrent2(para_subtractor_3_dcurrent2), .in_5(para_multiplexer_2_out_12),
    .Dcurrent1(para_subtractor_3_dcurrent1), .in_7(para_multiplexer_2_out_13),
    .Dcurrent0(para_subtractor_3_dcurrent0), .in_9(and_7_out), .out_10(para_multiplexer_3_out_10),
    .out_11(para_multiplexer_3_out_11), .out_12(para_multiplexer_3_out_12),
    .out_13(para_multiplexer_3_out_13), .Cout_final(Q1));
  not not_5 (Q0, para_subtractor_4_cout_final);
  para_subtractor para_subtractor_4 (
    .H0(and_4_out), .H1(and_3_out), .H2(and_2_out), .H3(and_1_out), .L0(and_9_out),
    .L1(para_multiplexer_3_out_13), .L2(para_multiplexer_3_out_12), .L3(para_multiplexer_3_out_11),
    .Dcurrent0(para_subtractor_4_dcurrent0), .Dcurrent1(para_subtractor_4_dcurrent1),
    .Dcurrent2(para_subtractor_4_dcurrent2), .Dcurrent3(para_subtractor_4_dcurrent3),
    .Cout_final(para_subtractor_4_cout_final));

  // Notes on the sheet:
  //   A/B
  //   Cout-f0
  //   Cout-f1
  //   Cout-f2
  //   Cout-f3
endmodule

module Multiblication (
  input  A3,
  input  A2,
  input  A1,
  input  A0,
  input  B0,
  input  B1,
  input  B2,
  input  B3,
  input  Enable,
  output Z7,
  output Z6,
  output Zero_Flag,
  output Z5,
  output Z4,
  output Z2,
  output Z1,
  output Z3,
  output Z0
);

  wire and_1_b0a, and_1_b1a, and_1_b2a, and_1_b3a, and_2_out, and_3_b0a, and_3_b1a, and_3_b2a, and_3_b3a,
       and_4_out, and_5_b0a, and_5_b1a, and_5_b2a, and_5_b3a, and_6_out, and_7_out, and_8_out, and_9_out,
       and_10_out, and_11_out, and_12_b1a, and_12_b2a, and_12_b3a, full_adder_2_carry_out, full_adder_2_sum,
       full_adder_3_carry_out, full_adder_4_carry_out, full_adder_4_sum, full_adder_5_carry_out,
       full_adder_6_carry_out, full_adder_6_sum, full_adder_7_carry_out, full_adder_7_sum,
       full_adder_8_carry_out, full_adder_8_sum, half_adder_1_carry_1, half_adder_1_sum,
       half_adder_2_carry_1, half_adder_3_carry_1, half_adder_4_carry_1;

  Zero_flag_of_multiplication zero_flag_of_multiplication_1 (
    .in_1(B3), .in_2(B2), .in_3(B1), .in_4(B0), .in_5(A0), .in_6(A1), .in_7(A2), .in_8(A3), .out_9(Zero_Flag));
  AND and_1 (
    .A(and_2_out), .B0(and_8_out), .B1(and_9_out), .B2(and_10_out), .B3(and_11_out), .B0A(and_1_b0a),
    .B1A(and_1_b1a), .B2A(and_1_b2a), .B3A(and_1_b3a));
  FULL_ADDER full_adder_1 (
    .CARRY_IN(full_adder_3_carry_out), .in_2(full_adder_2_carry_out), .in_3(and_1_b3a), .SUM(Z6),
    .CARRY_OUT(Z7));
  and and_2 (and_2_out, A3, Enable);
  FULL_ADDER full_adder_2 (
    .CARRY_IN(full_adder_4_carry_out), .in_2(half_adder_1_carry_1), .in_3(and_1_b2a), .SUM(full_adder_2_sum),
    .CARRY_OUT(full_adder_2_carry_out));
  FULL_ADDER full_adder_3 (
    .CARRY_IN(full_adder_5_carry_out), .in_2(full_adder_2_sum), .in_3(and_3_b3a), .SUM(Z5),
    .CARRY_OUT(full_adder_3_carry_out));
  AND and_3 (
    .A(and_4_out), .B0(and_8_out), .B1(and_9_out), .B2(and_10_out), .B3(and_11_out), .B0A(and_3_b0a),
    .B1A(and_3_b1a), .B2A(and_3_b2a), .B3A(and_3_b3a));
  HALF_ADDER half_adder_1 (
    .a(full_adder_6_carry_out), .b(and_1_b1a), .SUM(half_adder_1_sum), .CARRY_1(half_adder_1_carry_1));
  FULL_ADDER full_adder_4 (
    .CARRY_IN(full_adder_7_carry_out), .in_2(half_adder_1_sum), .in_3(and_3_b2a), .SUM(full_adder_4_sum),
    .CARRY_OUT(full_adder_4_carry_out));
  FULL_ADDER full_adder_5 (
    .CARRY_IN(half_adder_2_carry_1), .in_2(full_adder_4_sum), .in_3(and_5_b3a), .SUM(Z4),
    .CARRY_OUT(full_adder_5_carry_out));
  and and_4 (and_4_out, A2, Enable);
  FULL_ADDER full_adder_6 (
    .CARRY_IN(full_adder_8_carry_out), .in_2(and_3_b1a), .in_3(and_1_b0a), .SUM(full_adder_6_sum),
    .CARRY_OUT(full_adder_6_carry_out));
  FULL_ADDER full_adder_7 (
    .CARRY_IN(half_adder_3_carry_1), .in_2(and_5_b2a), .in_3(full_adder_6_sum), .SUM(full_adder_7_sum),
    .CARRY_OUT(full_adder_7_carry_out));
  HALF_ADDER half_adder_2 (.a(full_adder_7_sum), .b(and_12_b3a), .SUM(Z3), .CARRY_1(half_adder_2_carry_1));
  AND and_5 (
    .A(and_6_out), .B0(and_8_out), .B1(and_9_out), .B2(and_10_out), .B3(and_11_out), .B0A(and_5_b0a),
    .B1A(and_5_b1a), .B2A(and_5_b2a), .B3A(and_5_b3a));
  FULL_ADDER full_adder_8 (
    .CARRY_IN(half_adder_4_carry_1), .in_2(and_5_b1a), .in_3(and_3_b0a), .SUM(full_adder_8_sum),
    .CARRY_OUT(full_adder_8_carry_out));
  HALF_ADDER half_adder_3 (.a(full_adder_8_sum), .b(and_12_b2a), .SUM(Z2), .CARRY_1(half_adder_3_carry_1));
  and and_6 (and_6_out, A1, Enable);
  HALF_ADDER half_adder_4 (.a(and_12_b1a), .b(and_5_b0a), .SUM(Z1), .CARRY_1(half_adder_4_carry_1));
  and and_7 (and_7_out, A0, Enable);
  and and_8 (and_8_out, B0, Enable);
  and and_9 (and_9_out, B1, Enable);
  and and_10 (and_10_out, B2, Enable);
  and and_11 (and_11_out, B3, Enable);
  AND and_12 (
    .A(and_7_out), .B0(and_8_out), .B1(and_9_out), .B2(and_10_out), .B3(and_11_out), .B0A(Z0),
    .B1A(and_12_b1a), .B2A(and_12_b2a), .B3A(and_12_b3a));
endmodule

module Zero_flag_of_multiplication (
  input  in_1,
  input  in_2,
  input  in_3,
  input  in_4,
  input  in_5,
  input  in_6,
  input  in_7,
  input  in_8,
  output out_9
);

  wire zero_flag_1_out_5, zero_flag_2_out_5;

  zero_flag zero_flag_1 (.in_1(in_1), .in_2(in_2), .in_3(in_3), .in_4(in_4), .out_5(zero_flag_1_out_5));
  zero_flag zero_flag_2 (.in_1(in_5), .in_2(in_6), .in_3(in_7), .in_4(in_8), .out_5(zero_flag_2_out_5));
  or or_1 (out_9, zero_flag_1_out_5, zero_flag_2_out_5);
endmodule

module para_multiplexer (
  input  Cout_final,
  input  Dcurrent3,
  input  in_3,
  input  Dcurrent2,
  input  in_5,
  input  Dcurrent1,
  input  in_7,
  input  Dcurrent0,
  input  in_9,
  output out_10,
  output out_11,
  output out_12,
  output out_13
);

  Multiplexer_x multiplexer_x_1 (.S(Cout_final), .I0(in_3), .I1(Dcurrent3), .out_4(out_10));
  Multiplexer_x multiplexer_x_2 (.S(Cout_final), .I0(in_5), .I1(Dcurrent2), .out_4(out_11));
  Multiplexer_x multiplexer_x_3 (.S(Cout_final), .I0(in_7), .I1(Dcurrent1), .out_4(out_12));
  Multiplexer_x multiplexer_x_4 (.S(Cout_final), .I0(in_9), .I1(Dcurrent0), .out_4(out_13));
endmodule

module div_by_zero_flag (
  input  in_1,
  input  in_2,
  input  in_3,
  input  in_4,
  output out_5
);

  wire nor_1_out, nor_2_out;

  nor nor_1 (nor_1_out, in_1, in_2);
  nor nor_2 (nor_2_out, in_3, in_4);
  and and_1 (out_5, nor_1_out, nor_2_out);
endmodule

module zero_flag (
  input  in_1,
  input  in_2,
  input  in_3,
  input  in_4,
  output out_5
);

  wire nor_1_out, nor_2_out;

  nor nor_1 (nor_1_out, in_1, in_2);
  nor nor_2 (nor_2_out, in_3, in_4);
  and and_1 (out_5, nor_1_out, nor_2_out);
endmodule

module para_subtractor (
  input  H0,
  input  H1,
  input  H2,
  input  H3,
  input  L0,
  input  L1,
  input  L2,
  input  L3,
  output Dcurrent0,
  output Dcurrent1,
  output Dcurrent2,
  output Dcurrent3,
  output Cout_final
);

  wire full_subtractor_1_b_2, full_subtractor_2_b_2, full_subtractor_3_b_2;

  FULL_SUBTRACTOR full_subtractor_1 (.A(L0), .B(H0), .C(1'b0), .D(Dcurrent0), .B_2(full_subtractor_1_b_2));
  FULL_SUBTRACTOR full_subtractor_2 (
    .A(L1), .B(H1), .C(full_subtractor_1_b_2), .D(Dcurrent1), .B_2(full_subtractor_2_b_2));
  FULL_SUBTRACTOR full_subtractor_3 (
    .A(L2), .B(H2), .C(full_subtractor_2_b_2), .D(Dcurrent2), .B_2(full_subtractor_3_b_2));
  FULL_SUBTRACTOR full_subtractor_4 (.A(L3), .B(H3), .C(full_subtractor_3_b_2), .D(Dcurrent3), .B_2(Cout_final));
endmodule

module AND (
  input  A,
  input  B0,
  input  B1,
  input  B2,
  input  B3,
  output B0A,
  output B1A,
  output B2A,
  output B3A
);

  and and_1 (B0A, A, B0);
  and and_2 (B1A, A, B1);
  and and_3 (B2A, A, B2);
  and and_4 (B3A, A, B3);
endmodule

module HALF_ADDER (
  input  a,
  input  b,
  output SUM,
  output CARRY_1
);

  xor xor_1 (SUM, a, b);
  and and_1 (CARRY_1, a, b);

  // Notes on the sheet:
  //   sum
  //   C
endmodule

module FULL_ADDER (
  input  CARRY_IN,
  input  in_2,
  input  in_3,
  output SUM,
  output CARRY_OUT
);

  wire half_adder_1_carry_1, half_adder_1_sum, half_adder_2_carry_1;

  HALF_ADDER half_adder_1 (.a(in_2), .b(in_3), .SUM(half_adder_1_sum), .CARRY_1(half_adder_1_carry_1));
  HALF_ADDER half_adder_2 (.a(CARRY_IN), .b(half_adder_1_sum), .SUM(SUM), .CARRY_1(half_adder_2_carry_1));
  or or_1 (CARRY_OUT, half_adder_2_carry_1, half_adder_1_carry_1);
endmodule

module Multiplexer_x (
  input  S,
  input  I0,
  input  I1,
  output out_4
);

  wire and_1_out, and_2_out, not_1_out;

  not not_1 (not_1_out, S);
  and and_1 (and_1_out, not_1_out, I0);
  and and_2 (and_2_out, S, I1);
  or or_1 (out_4, and_1_out, and_2_out);
endmodule

module FULL_SUBTRACTOR (
  input  A,
  input  B,
  input  C,
  output D,
  output B_2
);

  wire and_1_out, and_2_out, and_3_out, not_1_out, or_1_out, xor_1_out;

  xor xor_1 (xor_1_out, A, B);
  not not_1 (not_1_out, A);
  xor xor_2 (D, xor_1_out, C);
  and and_1 (and_1_out, not_1_out, C);
  and and_2 (and_2_out, B, C);
  and and_3 (and_3_out, not_1_out, B);
  or or_1 (or_1_out, and_1_out, and_2_out);
  or or_2 (B_2, or_1_out, and_3_out);

  // Notes on the sheet:
  //   A-B
endmodule

module Binary_TO_BCD_CONVERTER (
  input  a3,
  input  a7,
  input  a6,
  input  a5,
  input  a4,
  input  a2,
  input  a0,
  input  a1,
  output out_9,
  output z,
  output z10,
  output z9,
  output z8,
  output z7,
  output z6,
  output z5,
  output z4,
  output z3,
  output z0,
  output z0_2
);

  wire shift_and_add_3_1_s0, shift_and_add_3_1_s1, shift_and_add_3_1_s2, shift_and_add_3_1_s3,
       shift_and_add_3_2_s0, shift_and_add_3_2_s1, shift_and_add_3_2_s2, shift_and_add_3_5_s0,
       shift_and_add_3_5_s1, shift_and_add_3_5_s2, shift_and_add_3_5_s3, shift_and_add_3_6_s0,
       shift_and_add_3_6_s1, shift_and_add_3_6_s2, shift_and_add_3_6_s3, shift_and_add_3_7_s0,
       shift_and_add_3_7_s1, shift_and_add_3_7_s2, shift_and_add_3_7_s3;

  SHIFT_AND_ADD_3 shift_and_add_3_1 (
    .a0(a5), .a1(a6), .a2(a7), .a3(1'b0), .s0(shift_and_add_3_1_s0), .s1(shift_and_add_3_1_s1),
    .s2(shift_and_add_3_1_s2), .s3(shift_and_add_3_1_s3));
  SHIFT_AND_ADD_3 shift_and_add_3_2 (
    .a0(shift_and_add_3_6_s3), .a1(shift_and_add_3_5_s3), .a2(shift_and_add_3_1_s3), .a3(1'b0),
    .s0(shift_and_add_3_2_s0), .s1(shift_and_add_3_2_s1), .s2(shift_and_add_3_2_s2), .s3(z10));
  SHIFT_AND_ADD_3 shift_and_add_3_3 (
    .a0(shift_and_add_3_7_s3), .a1(shift_and_add_3_2_s0), .a2(shift_and_add_3_2_s1),
    .a3(shift_and_add_3_2_s2), .s0(z6), .s1(z7), .s2(z8), .s3(z9));
  SHIFT_AND_ADD_3 shift_and_add_3_4 (
    .a0(a1), .a1(shift_and_add_3_7_s0), .a2(shift_and_add_3_7_s1), .a3(shift_and_add_3_7_s2), .s0(z0),
    .s1(z3), .s2(z4), .s3(z5));
  SHIFT_AND_ADD_3 shift_and_add_3_5 (
    .a0(a4), .a1(shift_and_add_3_1_s0), .a2(shift_and_add_3_1_s1), .a3(shift_and_add_3_1_s2),
    .s0(shift_and_add_3_5_s0), .s1(shift_and_add_3_5_s1), .s2(shift_and_add_3_5_s2), .s3(shift_and_add_3_5_s3));
  SHIFT_AND_ADD_3 shift_and_add_3_6 (
    .a0(a3), .a1(shift_and_add_3_5_s0), .a2(shift_and_add_3_5_s1), .a3(shift_and_add_3_5_s2),
    .s0(shift_and_add_3_6_s0), .s1(shift_and_add_3_6_s1), .s2(shift_and_add_3_6_s2), .s3(shift_and_add_3_6_s3));
  SHIFT_AND_ADD_3 shift_and_add_3_7 (
    .a0(a2), .a1(shift_and_add_3_6_s0), .a2(shift_and_add_3_6_s1), .a3(shift_and_add_3_6_s2),
    .s0(shift_and_add_3_7_s0), .s1(shift_and_add_3_7_s1), .s2(shift_and_add_3_7_s2), .s3(shift_and_add_3_7_s3));

  assign out_9 = 1'b0;
  assign z = 1'b0;
  assign z0_2 = a0;
endmodule

module SHIFT_AND_ADD_3 (
  input  a0,
  input  a1,
  input  a2,
  input  a3,
  output s0,
  output s1,
  output s2,
  output s3
);

  wire and_1_out, and_2_out, and_3_out, and_4_out, and_5_out, and_6_out, and_7_out, and_8_out, and_9_out,
       and_10_out, and_11_out, and_12_out, and_13_out, not_1_out, not_2_out, not_3_out, not_4_out, not_5_out,
       not_6_out, not_7_out, not_8_out, or_1_out, or_2_out, or_4_out;

  not not_1 (not_1_out, a0);
  not not_2 (not_2_out, a0);
  and and_1 (and_1_out, not_2_out, a1);
  not not_3 (not_3_out, a2);
  not not_4 (not_4_out, a0);
  and and_2 (and_2_out, not_4_out, a3);
  and and_3 (and_3_out, a1, not_5_out);
  not not_5 (not_5_out, a2);
  not not_6 (not_6_out, a0);
  and and_4 (and_4_out, not_6_out, not_7_out);
  not not_7 (not_7_out, a1);
  and and_5 (and_5_out, a1, a2);
  and and_6 (and_6_out, not_1_out, a3);
  and and_7 (and_7_out, and_1_out, a2);
  and and_8 (and_8_out, a0, not_3_out);
  not not_8 (not_8_out, a3);
  or or_1 (or_1_out, and_2_out, and_3_out);
  and and_9 (and_9_out, a0, a1);
  and and_10 (and_10_out, and_4_out, a2);
  and and_11 (and_11_out, a0, a3);
  or or_2 (or_2_out, a3, and_5_out);
  or or_3 (s3, or_2_out, and_12_out);
  and and_12 (and_12_out, a0, a2);
  or or_4 (or_4_out, and_6_out, and_7_out);
  and and_13 (and_13_out, and_8_out, not_8_out);
  or or_5 (s1, or_1_out, and_9_out);
  or or_6 (s2, and_10_out, and_11_out);
  or or_7 (s0, or_4_out, and_13_out);
endmodule

module BCD_TO_7_SEGMENT (
  input  B,
  input  C,
  input  D,
  input  A,
  output a_2,
  output b_2,
  output c_2,
  output d_2,
  output e,
  output f,
  output g
);

  wire and_1_out, and_2_out, and_3_out, and_4_out, and_5_out, and_6_out, and_7_out, and_8_out, and_9_out,
       not_1_out, not_2_out, not_3_out, or_1_out, or_2_out, or_3_out, or_4_out, or_5_out, or_8_out, or_9_out,
       or_10_out, or_11_out, or_12_out, or_14_out;

  not not_1 (not_1_out, B);
  not not_2 (not_2_out, C);
  not not_3 (not_3_out, D);
  and and_1 (and_1_out, C, not_3_out);
  and and_2 (and_2_out, not_1_out, C);
  and and_3 (and_3_out, B, D);
  and and_4 (and_4_out, not_1_out, not_3_out);
  and and_5 (and_5_out, C, D);
  and and_6 (and_6_out, not_2_out, not_3_out);
  and and_7 (and_7_out, B, not_2_out);
  and and_8 (and_8_out, B, not_3_out);
  and and_9 (and_9_out, D, and_7_out);
  or or_1 (or_1_out, and_3_out, and_4_out);
  or or_2 (or_2_out, A, C);
  or or_3 (or_3_out, and_5_out, not_1_out);
  or or_4 (or_4_out, B, not_2_out);
  or or_5 (or_5_out, and_4_out, A);
  or or_6 (a_2, or_1_out, or_2_out);
  or or_7 (b_2, or_3_out, and_6_out);
  or or_8 (or_8_out, and_2_out, and_9_out);
  or or_9 (or_9_out, and_6_out, and_7_out);
  or or_10 (or_10_out, and_8_out, A);
  or or_11 (or_11_out, and_7_out, and_1_out);
  or or_12 (or_12_out, and_2_out, A);
  or or_13 (c_2, or_4_out, D);
  or or_14 (or_14_out, or_5_out, and_1_out);
  or or_15 (d_2, or_14_out, or_8_out);
  or or_16 (f, or_9_out, or_10_out);
  or or_17 (g, or_11_out, or_12_out);
  or or_18 (e, and_4_out, and_1_out);
endmodule

module _4_BIT_PARALLEL_ADDER (
  input  Bo,
  input  Ao,
  input  B1,
  input  A1,
  input  B2,
  input  A2,
  input  B3,
  input  A3,
  input  S,
  output C4,
  output S0,
  output S1,
  output S2,
  output S3
);

  wire full_adder_with_diff_implementation_1_carry, full_adder_with_diff_implementation_2_carry,
       full_adder_with_diff_implementation_3_carry, xor_1_out, xor_2_out, xor_3_out, xor_4_out;

  xor xor_1 (xor_1_out, Bo, S);
  FULL_ADDER_WITH_DIFF_IMPLEMENTATION full_adder_with_diff_implementation_1 (
    .A(Ao), .B(xor_1_out), .Cp(S), .carry(full_adder_with_diff_implementation_1_carry), .Result(S0));
  xor xor_2 (xor_2_out, B1, S);
  FULL_ADDER_WITH_DIFF_IMPLEMENTATION full_adder_with_diff_implementation_2 (
    .A(A1), .B(xor_2_out), .Cp(full_adder_with_diff_implementation_1_carry),
    .carry(full_adder_with_diff_implementation_2_carry), .Result(S1));
  xor xor_3 (xor_3_out, B2, S);
  FULL_ADDER_WITH_DIFF_IMPLEMENTATION full_adder_with_diff_implementation_3 (
    .A(A2), .B(xor_3_out), .Cp(full_adder_with_diff_implementation_2_carry),
    .carry(full_adder_with_diff_implementation_3_carry), .Result(S2));
  xor xor_4 (xor_4_out, B3, S);
  FULL_ADDER_WITH_DIFF_IMPLEMENTATION full_adder_with_diff_implementation_4 (
    .A(A3), .B(xor_4_out), .Cp(full_adder_with_diff_implementation_3_carry), .carry(C4), .Result(S3));
endmodule

module FULL_ADDER_WITH_DIFF_IMPLEMENTATION (
  input  A,
  input  B,
  input  Cp,
  output carry,
  output Result
);

  wire and_1_out, and_2_out, xor_1_out, xor_2_out;

  and and_1 (and_1_out, A, B);
  xor xor_1 (xor_1_out, A, B);
  and and_2 (and_2_out, xor_1_out, Cp);
  xor xor_2 (xor_2_out, A, B);
  or or_1 (carry, and_1_out, and_2_out);
  xor xor_3 (Result, xor_2_out, Cp);
endmodule
